# Fritzing sketch station PCB v1+ (saved by Fritzing 0.9.3b)
circuit board: 8cm x 8cm
breadboards: 1

parts:
  Arduino_Nano = Arduino Nano (Rev3.0)
  D8 = male pin header, 3 pins [form="♂ (male)"]
  D6* = male pin header, 3 pins [form="♂ (male)"]
  D7 = male pin header, 3 pins [form="♂ (male)"]
  D2 = male pin header, 3 pins [form="♂ (male)"]
  D5* = male pin header, 3 pins [form="♂ (male)"]
  D4 = male pin header, 3 pins [form="♂ (male)"]
  D3* = male pin header, 3 pins [form="♂ (male)"]
  I2C = male pin header, 4 pins [form="♂ (male)"]
  I2C_2 = male pin header, 4 pins [form="♂ (male)"]
  NRF24l01+ = NRF24L01+ Breakout Board
  A2 = male pin header, 3 pins [form="♂ (male)"]
  A3 = male pin header, 3 pins [form="♂ (male)"]
  A1 = male pin header, 3 pins [form="♂ (male)"]
  A0 = male pin header, 3 pins [form="♂ (male)"]
  R7 = Resistor [tolerance=±5% resistance=220 package=THT]
  R8 = Resistor [tolerance=±5% resistance=220 package=THT]
  R9 = Resistor [tolerance=±5% resistance=220 package=THT]
  R10 = Resistor [tolerance=±5% resistance=220 package=THT]
  R11 = Resistor [tolerance=±5% resistance=220 package=THT]
  R12 = Resistor [tolerance=±5% resistance=220 package=THT]
  R13 = Resistor [tolerance=±5% resistance=220 package=THT]
  ZS-042_RTC1 = ZS-042 RTC Module
  U1 = MCP73831 [package=sot23-5]
  BAT1 = 18650 battery holder [package=battery-18650-kit]
  C1 = Electrolytic Capacitor [capacitance=10μF package="0605 [SMD, electrolytic]"]
  U2 = USB_AB [package=usb-ab-micro-smd]
  LED1 = LEDs [package=led10mm]
  R14 = Resistor [tolerance=±5% resistance=1k package=THT]
  LED2 = LEDs [package=led10mm]
  R15 = Resistor [tolerance=±5% resistance=1k package=THT]
  C2 = Electrolytic Capacitor [capacitance=10μF package="0605 [SMD, electrolytic]"]
  R16 = Resistor [tolerance=±5% resistance=2k package=THT]

nets (from the breadboard view):
  GND: Arduino_Nano.GND, D8.pin1, D6*.pin1, D7.pin1, D2.pin1, D5*.pin1, D4.pin1, D3*.pin1, I2C.pin1, I2C_2.pin1, NRF24l01+.GND, A2.pin3, A3.pin3, A1.pin3, A0.pin3, R7.Pin_0, R8.Pin_0, R9.Pin_0, R10.Pin_0, R11.Pin_0, R12.Pin_0, R13.Pin_0, ZS-042_RTC1.GND, U1.VSS, BAT1.-, C1.+, U2.GND, R14.Pin_1, R15.Pin_1, C2.+, R16.Pin_0
  N1: Arduino_Nano.D2, D2.pin3, R7.Pin_1
  N2: Arduino_Nano.D3, D3*.pin3, R10.Pin_1
  N3: Arduino_Nano.D4, D4.pin3, R8.Pin_1
  N4: Arduino_Nano.D5, D5*.pin3, R11.Pin_1
  N5: Arduino_Nano.D6, D6*.pin3, R12.Pin_1
  N6: Arduino_Nano.D7, D7.pin3, R9.Pin_1
  N7: Arduino_Nano.D8, D8.pin3, R13.Pin_1
  N8: Arduino_Nano.D9, NRF24l01+.CE
  N9: Arduino_Nano.D10, NRF24l01+.CS
  N10: Arduino_Nano.D11/MOSI, NRF24l01+.MOSI
  N11: Arduino_Nano.D12/MISO, NRF24l01+.MISO
  5V: Arduino_Nano.5V, D8.pin2, D6*.pin2, D7.pin2, D2.pin2, D5*.pin2, D4.pin2, D3*.pin2, I2C.pin2, I2C_2.pin2, A2.pin2, A3.pin2, A1.pin2, A0.pin2, ZS-042_RTC1.VCC
  N12: Arduino_Nano.A5, I2C.pin4, I2C_2.pin4, ZS-042_RTC1.SCL
  N13: Arduino_Nano.A4, I2C.pin3, I2C_2.pin3, ZS-042_RTC1.SDA
  N14: Arduino_Nano.A3, A3.pin1
  N15: Arduino_Nano.A2, A2.pin1
  N16: Arduino_Nano.A1, A1.pin1
  N17: Arduino_Nano.A0, A0.pin1
  3V3: Arduino_Nano.3V3, NRF24l01+.VCC
  N18: Arduino_Nano.D13/SCK, NRF24l01+.SCK
  N19: U1.STAT, LED1.A
  N20: U1.VBAT, BAT1.+, C1.-
  N21: U1.VIN, U2.VBUS, LED2.A, R15.Pin_0, C2.-
  N22: U1.PROG, R16.Pin_1
  N23: LED1.C, R14.Pin_0

notes:
  Remote Buttons
  IJssel Koster
  V1

custom parts:
  18650 battery holder: 18650 Battery Holder
