# Fritzing sketch station v1 (saved by Fritzing 0.9.3b)
circuit board: 8cm x 8cm

parts:
  Arduino_Nano = Arduino Nano (Rev3.0)
  D8 = male pin header, 3 pins [form="♂ (male)"]
  D6* = male pin header, 3 pins [form="♂ (male)"]
  D7 = male pin header, 3 pins [form="♂ (male)"]
  D2 = male pin header, 3 pins [form="♂ (male)"]
  D5* = male pin header, 3 pins [form="♂ (male)"]
  D4 = male pin header, 3 pins [form="♂ (male)"]
  D3* = male pin header, 3 pins [form="♂ (male)"]
  I2C = male pin header, 4 pins [form="♂ (male)"]
  I2C_2 = male pin header, 4 pins [form="♂ (male)"]
  Vin = female pin header, 2 pins [form="♀ (female)"]
  NRF24l01+ = NRF24L01+ Breakout Board
  A2 = male pin header, 3 pins [form="♂ (male)"]
  ZS-042_RTC1 = ZS-042 RTC Module
  A3 = male pin header, 3 pins [form="♂ (male)"]
  A1 = male pin header, 3 pins [form="♂ (male)"]
  A0 = male pin header, 3 pins [form="♂ (male)"]

nets:
  GND: Arduino_Nano.GND, D8.pin1, D6*.pin1, D7.pin1, D2.pin1, D5*.pin1, D4.pin1, D3*.pin1, I2C.pin1, I2C_2.pin1, Vin.pin2, NRF24l01+.GND, A2.pin3, ZS-042_RTC1.GND, A3.pin3, A1.pin3, A0.pin3
  N1: Arduino_Nano.D2, D2.pin3
  N2: Arduino_Nano.D3, D3*.pin3
  N3: Arduino_Nano.D4, D4.pin3
  N4: Arduino_Nano.D5, D5*.pin3
  N5: Arduino_Nano.D6, D6*.pin3
  N6: Arduino_Nano.D7, D7.pin3
  N7: Arduino_Nano.D8, D8.pin3
  N8: Arduino_Nano.D9, NRF24l01+.CE
  N9: Arduino_Nano.D10, NRF24l01+.CS
  N10: Arduino_Nano.D11/MOSI, NRF24l01+.MOSI
  N11: Arduino_Nano.D12/MISO, NRF24l01+.MISO
  N12: Arduino_Nano.VIN, Vin.pin1
  5V: Arduino_Nano.5V, D8.pin2, D6*.pin2, D7.pin2, D2.pin2, D5*.pin2, D4.pin2, D3*.pin2, I2C.pin2, I2C_2.pin2, A2.pin2, ZS-042_RTC1.VCC, A3.pin2, A1.pin2, A0.pin2
  N13: Arduino_Nano.A5, I2C.pin4, I2C_2.pin4, ZS-042_RTC1.SCL
  N14: Arduino_Nano.A4, I2C.pin3, I2C_2.pin3, ZS-042_RTC1.SDA
  N15: Arduino_Nano.A3, A3.pin1
  N16: Arduino_Nano.A2, A2.pin1
  N17: Arduino_Nano.A1, A1.pin1
  N18: Arduino_Nano.A0, A0.pin1
  3V3: Arduino_Nano.3V3, NRF24l01+.VCC
  N19: Arduino_Nano.D13/SCK, NRF24l01+.SCK
